# Fritzing sketch BatLogger (saved by Fritzing 0.8.7b)
circuit board: 8.69994cm x 4.10471cm
breadboards: 1

parts:
  MIC = Microphone
  R1 = Resistor [tolerance=±5% resistance=10k package=THT]
  Q1 = NPN-Transistor [part_number=2N3904 package="TO92 [THT]"]
  Q2 = NPN-Transistor [part_number=2N3904 package="TO92 [THT]"]
  Q3 = NPN-Transistor [part_number=2N3904 package="TO92 [THT]"]
  R3 = Resistor [tolerance=±5% resistance=18k package=THT]
  R2 = Resistor [tolerance=±5% resistance=100k package=THT]
  R5 = Resistor [tolerance=±5% resistance=4.7k package=THT]
  R6 = Resistor [tolerance=±5% resistance=47 package=THT]
  R4 = Resistor [tolerance=±5% resistance=47k package=THT]
  R7 = Resistor [tolerance=±5% resistance=10k package=THT]
  R8 = Resistor [tolerance=±5% resistance=100k package=THT]
  R11 = Resistor [tolerance=±5% resistance=4.7k package=THT]
  R10 = Resistor [tolerance=±5% resistance=47k package=THT]
  R9 = Resistor [tolerance=±5% resistance=18k package=THT]
  R12 = Resistor [tolerance=±5% resistance=47 package=THT]
  -5V+ = Screw terminal - 2 pins [package=THT]
  IC1 = IC, DIP package, 14 pins [chip_label=CD4024]
  U1 = atmega328 [package=dip]
  X1 = Crystal [frequency="16 Mhz" package=THT]
  RESET = Pushbutton [package="[THT]"]
  R13 = Resistor [tolerance=±5% resistance=10k package=THT]
  PRG = male pin header, 6 pins [form="♂ (male)"]
  RST = male pin header, 2 pins [form="♂ (male)"]
  MON = male pin header, 2 pins [form="♂ (male)"]
  C8 = Electrolytic Capacitor [capacitance=330µF package="100 mil [THT, electrolytic]"]
  R14 = Resistor [tolerance=±5% resistance=220 package=THT]
  R15 = Resistor [tolerance=±5% resistance=220 package=THT]
  R16 = Resistor [tolerance=±5% resistance=220 package=THT]
  LED1 = LED - 5mm [color="Red (633nm)" package="5 mm [THT]"]
  LED2 = LED - 5mm [color="Red (633nm)" package="5 mm [THT]"]
  LED3 = LED - 5mm [color="Red (633nm)" package="5 mm [THT]"]
  T1 = LM35 Temperature Sensor [package="TO92 [THT]"]
  R17 = Resistor [tolerance=±5% resistance=220 package=THT]
  R18 = Photocell (LDR) [package=THT]
  S1 = Pushbutton [package="[THT]"]
  S2 = Pushbutton [package="[THT]"]
  RTC = female pin header, 4 pins [form="♀ (female)"]
  SD_CARD = male pin header, 6 pins [form="♂ (male)"]
  Q4 = NPN-Transistor [package="TO92 [THT]"]
  R19 = Resistor [tolerance=±5% resistance=2.2k package=THT]
  C5 = Ceramic Capacitor [capacitance=22pF package="200 mil [THT, multilayer]"]
  C6 = Ceramic Capacitor [capacitance=22pF package="200 mil [THT, multilayer]"]
  C4 = Ceramic Capacitor [capacitance=100nF package="200 mil [THT, multilayer]"]
  C2 = Ceramic Capacitor [capacitance=100nF package="200 mil [THT, multilayer]"]
  C1 = Ceramic Capacitor [capacitance=1nF package="200 mil [THT, multilayer]"]
  C3 = Ceramic Capacitor [capacitance=1nF package="200 mil [THT, multilayer]"]
  C7 = Ceramic Capacitor [capacitance=100nF package="200 mil [THT, multilayer]"]
  A3A0 = male pin header, 2 pins [form="♂ (male)"]
  D4 = female pin header, 1 pin [form="♀ (female)"]

nets:
  GND: MIC.pin1, R3.Pin_1, R5.Pin_1, R7.Pin_0, R11.Pin_1, R9.Pin_1, -5V+.pin2, IC1.pin7, U1.GND, RESET.Pin_3, RESET.Pin_4, PRG.pin6, RST.pin2, MON.pin1, C8.-, LED1.cathode, LED2.cathode, LED3.cathode, T1.GND, R17.Pin_0, S1.Pin_3, S1.Pin_4, S2.Pin_3, S2.Pin_4, RTC.pin4, Q4.E, C5.0, C6.0, C4.1, C2.1
  N1: MIC.pin2, R1.Pin_0, C1.1
  N2: R1.Pin_1, Q2.C, R2.Pin_0, R4.Pin_0, R8.Pin_1, R10.Pin_0, -5V+.pin1, IC1.pin14, U1.VCC, U1.AVCC, U1.AREF, R13.Pin_0, PRG.pin4, C8.+, T1.+Vs, R18.pin_1, RTC.pin3, SD_CARD.pin2
  N3: Q1.E, R5.Pin_0, R6.Pin_0
  N4: Q1.B, R3.Pin_0, R2.Pin_1, C1.0
  N5: Q1.C, Q2.B, R4.Pin_1
  N6: Q2.E, R7.Pin_1, C3.0
  N7: Q3.E, R11.Pin_0, R12.Pin_0
  N8: Q3.B, R8.Pin_0, R9.Pin_0, C3.1
  N9: Q3.C, R10.Pin_1, IC1.pin1
  N10: R6.Pin_1, C2.0
  N11: R12.Pin_1, C4.0
  N12: IC1.pin2, RST.pin1
  N13: IC1.pin3, U1.D2
  N14: IC1.pin4, MON.pin2
  N15: U1.RESET, RESET.Pin_1, RESET.Pin_2, R13.Pin_1, C7.0
  N16: U1.D0_(RX), PRG.pin3
  N17: U1.D1_(TX), PRG.pin2
  N18: U1.D3_(PWM), R19.Pin_0
  N19: U1.D4, D4.pin1
  N20: U1.XLAT1, X1.pin_0, C6.1
  N21: U1.XLAT2, X1.pin_1, C5.1
  N22: U1.D5_(PWM), R14.Pin_0
  N23: U1.D6_(PWM), R15.Pin_0
  N24: U1.D7, R16.Pin_0
  N25: U1.D8, S2.Pin_1, S2.Pin_2
  N26: U1.D9_(PWM), S1.Pin_1, S1.Pin_2
  N27: U1.D10_(PWM), SD_CARD.pin6
  N28: U1.D11_(PWM), SD_CARD.pin4
  N29: U1.D12, SD_CARD.pin3
  N30: U1.D13, SD_CARD.pin5
  N31: U1.A0, A3A0.pin1
  N32: U1.A1, T1.Vout
  N33: U1.A2, R17.Pin_1, R18.pin_0
  N34: U1.A3, A3A0.pin2
  N35: U1.A4, RTC.pin2
  N36: U1.A5, RTC.pin1
  N37: PRG.pin1, C7.1
  N38: R14.Pin_1, LED1.anode
  N39: R15.Pin_1, LED3.anode
  N40: R16.Pin_1, LED2.anode
  N41: SD_CARD.pin1, Q4.C
  N42: Q4.B, R19.Pin_1

notes:
  BatLogger V0.1
  GND
  NC
  VCC
  TX
  RX
  RST
  SDA
  SCL
  MISO
  MOSI
  SCK
  CS
