# Fritzing sketch BatLoggerLm386 (saved by Fritzing 0.9.0b)
circuit board: 7.60612cm x 4.11142cm
breadboards: 1

parts:
  MIC = Microphone
  R1 = Resistor [tolerance=±5% resistance=10k package=THT]
  -5V+ = Screw terminal - 2 pins [package=THT]
  U1 = atmega328 [package=dip]
  X1 = Crystal [frequency="16 Mhz" package=THT]
  RESET = Pushbutton [package="[THT]"]
  R13 = Resistor [tolerance=±5% resistance=10k package=THT]
  PRG = male pin header, 6 pins [form="♂ (male)"]
  R14 = Resistor [tolerance=±5% resistance=220 package=THT]
  R15 = Resistor [tolerance=±5% resistance=220 package=THT]
  R16 = Resistor [tolerance=±5% resistance=220 package=THT]
  LED3 = LED - 5mm [color="Red (633nm)" package="5 mm [THT]"]
  LED1 = LED - 5mm [color="Red (633nm)" package="5 mm [THT]"]
  LED2 = LED - 5mm [color="Red (633nm)" package="5 mm [THT]"]
  T1 = LM35 Temperature Sensor [package="TO92 [THT]"]
  R17 = Resistor [tolerance=±5% resistance=10k package=THT]
  R18 = Photocell (LDR) [package=THT]
  S1 = Pushbutton [package="[THT]"]
  S2 = Pushbutton [package="[THT]"]
  RTC = female pin header, 4 pins [form="♀ (female)"]
  SD_CARD = male pin header, 6 pins [form="♂ (male)"]
  R19 = Resistor [tolerance=±5% resistance=2.2k package=THT]
  C5 = Ceramic Capacitor [capacitance=22pF package="200 mil [THT, multilayer]"]
  C6 = Ceramic Capacitor [capacitance=22pF package="200 mil [THT, multilayer]"]
  C7 = Ceramic Capacitor [capacitance=100nF package="200 mil [THT, multilayer]"]
  Q4 = NPN-Transistor [part_number=BC547 package="TO92 [THT]"]
  D6 = male pin header, 1 pin [form="♂ (male)"]
  C9 = Electrolytic Capacitor [capacitance=10µF package="100 mil [THT, electrolytic]"]
  C10 = Electrolytic Capacitor [capacitance=1µF package="100 mil [THT, electrolytic]"]
  C11 = Electrolytic Capacitor [capacitance=10µF package="100 mil [THT, electrolytic]"]
  R20 = Resistor [tolerance=±5% resistance=100 package=THT]
  IC1 = IC, DIP package, 8 pins [chip_label=IC part_number=LM386]
  IC2 = IC, DIP package, 8 pins [chip_label=IC part_number=LM386]
  C14 = Electrolytic Capacitor [capacitance=1µF package="100 mil [THT, electrolytic]"]
  C13 = Electrolytic Capacitor [capacitance=10µF package="100 mil [THT, electrolytic]"]
  R21 = Resistor [tolerance=±5% resistance=100 package=THT]
  R22 = Trimmer Potentiometer [maximum_resistance=10kΩ package=THT]
  C8 = Electrolytic Capacitor [capacitance=1mF package="200 mil [THT, electrolytic]"]
  C12 = Ceramic Capacitor [capacitance=22nF package="200 mil [THT, multilayer]"]

nets:
  GND: MIC.pin1, -5V+.pin2, U1.GND, RESET.Pin_3, RESET.Pin_4, PRG.pin6, LED3.cathode, LED1.cathode, LED2.cathode, T1.GND, R17.Pin_0, S1.Pin_3, S1.Pin_4, S2.Pin_3, S2.Pin_4, RTC.pin4, C5.0, C6.0, Q4.E, C10.-, IC1.pin2, IC1.pin4, IC2.pin2, IC2.pin4, C14.-, R21.Pin_1, C8.-
  N1: MIC.pin2, R1.Pin_0, C9.+
  N2: R1.Pin_1, -5V+.pin1, U1.VCC, U1.AVCC, U1.AREF, R13.Pin_0, PRG.pin4, T1.+Vs, R18.pin_1, RTC.pin3, SD_CARD.pin2, IC1.pin6, IC2.pin6, C8.+
  N3: U1.RESET, RESET.Pin_1, RESET.Pin_2, R13.Pin_1, C7.0
  N4: U1.D0_(RX), PRG.pin3
  N5: U1.D1_(TX), PRG.pin2
  N6: U1.D2, S2.Pin_1
  N7: U1.D3_(PWM), R14.Pin_0
  N8: U1.D4, D6.pin1
  N9: U1.XLAT1, X1.pin_0, C6.1
  N10: U1.XLAT2, X1.pin_1, C5.1
  N11: U1.D5_(PWM), IC2.pin5
  N12: U1.D6_(PWM), R15.Pin_0
  N13: U1.D7, R19.Pin_0
  N14: U1.D8, S1.Pin_1, S1.Pin_2
  N15: U1.D9_(PWM), R16.Pin_0
  N16: U1.D10_(PWM), SD_CARD.pin6
  N17: U1.D11_(PWM), SD_CARD.pin4
  N18: U1.D12, SD_CARD.pin3
  N19: U1.D13, SD_CARD.pin5
  N20: U1.A1, T1.Vout
  N21: U1.A2, R17.Pin_1, R18.pin_0
  N22: U1.A4, RTC.pin2
  N23: U1.A5, RTC.pin1
  N24: PRG.pin1, C7.1
  N25: R14.Pin_1, LED3.anode
  N26: R15.Pin_1, LED2.anode
  N27: R16.Pin_1, LED1.anode
  N28: SD_CARD.pin1, Q4.C
  N29: R19.Pin_1, Q4.B
  N30: C9.-, IC1.pin3
  N31: C10.+, IC1.pin7
  N32: C11.-, IC1.pin8
  N33: C11.+, R20.Pin_1
  N34: R20.Pin_0, IC1.pin1
  N35: IC1.pin5, C12.0
  N36: IC2.pin1, R22.leg2
  N37: IC2.pin3, R21.Pin_0, C12.1
  N38: IC2.pin7, C14.+
  N39: IC2.pin8, C13.-
  N40: C13.+, R22.leg1, R22.wiper

notes:
  Bat
  GND
  NC
  VCC
  TX
  RX
  RST
  SDA
  SCL
  MISO
  MOSI
  SCK
  CS
  V0.3
  Logger
